# Fritzing sketch WATERING_SYSTEM (saved by Fritzing 0.9.3b)
circuit board: 4.12514cm x 4.92007cm

parts:
  U1 = NodeMCU V1.0
  U2 = Vibration Motor- ROB-08449 [package=vibe-motor-10mm]
  Q1 = NPN-Transistor [package="TO92 [THT]"]
  VCC1 = 4 x AAA Battery Mount
  Part1 = FC-28 Soil Hygrometer Module

nets:
  N1: U1.D0, Q1.B
  N2: U1.D2, Part1.DO
  3V3: U1.3V3, Part1.VCC
  GND: U1.GND, Q1.C, VCC1.-, Part1.GND
  N3: U1.Vin, U2.-, VCC1.+
  N4: U2.+, Q1.E

custom parts:
  NodeMCU V1.0: ESP8266 based NodeMCU
  FC-28 Soil Hygrometer Module: The FC-28 is a soil hygrometer module that uses the Texas Instruments LM393 comparator chip to provide an analog measurement of soil humidity. The digital output is high when soil moisture is over a certain threshold, as determined by adjusting the potentiometer.
